# Fritzing sketch Circuit_DHT11_TSL2561 (saved by Fritzing 0.9.2b)
breadboards: 1

parts:
  Raspberry_Pi1 = Raspberry Pi 2
  RHT1 = Humidity and Temperature Sensor RHT03
  R1 = Resistor [tolerance=±5% resistance=220 package="2010 [SMD]"]
  U2 = SI1120 [package=odfn]

nets:
  3V3: Raspberry_Pi1.3v3, RHT1.Vcc, R1.Pin_0, U2.VDD
  N1: Raspberry_Pi1.GPIO2, U2.STX
  N2: Raspberry_Pi1.GPIO3, U2.TXO
  N3: Raspberry_Pi1.GPIO4, RHT1.Data-signal, R1.Pin_1
  N4: Raspberry_Pi1.GND, RHT1.GND_2, U2.PRX
