# Fritzing sketch Circuit_automation (saved by Fritzing 0.9.2b)
breadboards: 1

parts:
  Raspberry_Pi1 = Raspberry Pi 2
  R1 = Resistor [tolerance=±5% resistance=220 package="2010 [SMD]"]
  U2 = SI1120 [package=odfn]
  DHT1 = DHT11 Humitidy and Temperature Sensor
  Q1 = TIP120 Hi-Current Darlington Transistor
  R2 = Resistor [tolerance=±5% resistance=1.2k package="2010 [SMD]"]
  D1 = Rectifier Diode [part_number=1N4001 package="Melf DO-213 AB [SMD]"]
  VCC1 = 4 x AAA Battery Mount
  NEOPIXEL1 = Neopixel Strip -- White (30/m)

nets:
  N1: Raspberry_Pi1.3v3, R1.Pin_0, U2.TXO, DHT1.DATA
  N2: Raspberry_Pi1.GPIO2, U2.STX
  N3: Raspberry_Pi1.GPIO3, U2.VDD
  N4: Raspberry_Pi1.GPIO4, R1.Pin_1, DHT1.VDD
  N5: Raspberry_Pi1.GPIO6, R2.Pin_0
  GND: Raspberry_Pi1.GND, U2.TXGD, DHT1.GND, Q1.EMITTER, D1.anode, VCC1.-
  N6: Q1.BASE, R2.Pin_1
  N7: Q1.COLLECTOR, D1.cathode, NEOPIXEL1.GND
  N8: VCC1.+, NEOPIXEL1.+5V

custom parts:
  DHT11 Humitidy and Temperature Sensor: DHT11 Humidity and Temperature Sensor
  Neopixel Strip -- White (30/m): These NeoPixel strips have 30 digitally-addressable pixel LEDs per meter and are very affordable and are only 12.5 mm wide, 10 mm if you remove the strip from the casing.
